# Fritzing sketch TinyMusic (saved by Fritzing 0.9.2b)
circuit board: 2.43cm x 2.43cm
breadboards: 1

parts:
  U1 = attiny85 [package=dip]
  C1 = Ceramic Capacitor [capacitance=100nF package="100 mil [THT, multilayer]"]
  S1 = Pushbutton [package="[THT]"]
  BUZ = Buzzer 12mm [package=buzzer-12mm-ns-kit]
  LED1 = LED - 5mm [color="Red (633nm)" package="5 mm [THT]"]
  R2 = Resistor [tolerance=±5% resistance=1k package=THT]
  CR2032 = CR2032
  R1 = Resistor [tolerance=±5% resistance=10k package=THT]
  R3 = Resistor [tolerance=±5% resistance=10k package=THT]
  R4 = Resistor [tolerance=±5% resistance=1k package=THT]
  LED2 = LED - 3mm [color="Red (633nm)" package="3 mm [THT]"]

nets:
  N1: U1.Pin_1, R3.Pin_0
  N2: U1.Pin_2, R4.Pin_1
  N3: U1.Pin_3, R2.Pin_1
  GND: U1.Pin_4, C1.0, LED1.cathode, CR2032.-, R1.Pin_1, LED2.cathode
  N4: U1.Pin_5, S1.Pin_1, S1.Pin_2, R1.Pin_0
  N5: U1.Pin_6, BUZ.2
  N6: U1.Pin_7, BUZ.1
  N7: U1.Pin_8, C1.1, S1.Pin_3, S1.Pin_4, CR2032.+, R3.Pin_1
  N8: LED1.anode, R2.Pin_0
  N9: R4.Pin_0, LED2.anode

notes:
  Josepa y Paco
  16-07-2016
  TinyMusic, Key chain music player with two leds and a buzzer., 1.0
  *TinyMusic: MinorSwing*

custom parts:
  CR2032: CR2032 coin cell PCB adapter
